# Fritzing sketch DRV8825 - Arduino Uno (saved by Fritzing 0.9.3b)

parts:
  DRV_1 = DRV 8825 Stepper Motor Carrier, High Current [part_number="DRV 8825"]
  Part1 = Arduino Uno (Rev3) - ICSP

nets:
  N1: DRV_1.RESET, DRV_1.SLEEP, Part1.5V
  N2: DRV_1.STEP, Part1.D9_PWM
  N3: DRV_1.DIRECTION, Part1.D8
  N4: DRV_1.GROUND_LOG, Part1.GND
