# Fritzing sketch arduino (saved by Fritzing 0.9.3b)

parts:
  Part1 = Arduino Uno (Rev3)
  LED3 = RGB LED (com. cathode, rbg) [package="5 mm [THT]"]

nets:
  N1: Part1.D8, LED3.red_anode
  N2: Part1.D9_PWM, LED3.green_anode
  N3: Part1.D10_PWM/SS, LED3.blue_anode
  N4: Part1.GND, LED3.common_cathode
